// Logisim project au.circ as structural Verilog: 1 circuit, main circuit ALU
module ALU (
  input  [31:0] reg1,
  input  [31:0] reg2,
  input  zero,
  input  [4:0] shiftAmount,
  output [31:0] result
);

  wire undriven, undriven_2;
  wire [3:0] undriven_5;
  wire [4:0] multiplexer_1_out, multiplexer_2_out;
  wire [31:0] adder_1_out, and_1_out, comparator_1_lt, divider_1_out, multiplier_1_out, nor_1_out, or_1_out,
       shifter_1_out, shifter_2_out, shifter_3_out, subtractor_1_out, undriven_3, undriven_4, xor_1_out;

  Multiplexer #(.width(5)) multiplexer_1 (.in0(reg1[4:0]), .in1(shiftAmount), .out(multiplexer_1_out), .sel(undriven));
  Multiplexer #(.width(5)) multiplexer_2 (
    .in0(reg1[4:0]), .in1(shiftAmount), .out(multiplexer_2_out), .sel(undriven_2));
  Adder #(.width(32)) adder_1 (.a(reg1), .b(reg2), .out(adder_1_out));  // open: cin, cout
  Subtractor #(.width(32)) subtractor_1 (.a(reg1), .b(reg2), .out(subtractor_1_out));  // open: bin, bout
  assign xor_1_out = reg1 ^ reg2;  // XOR_Gate xor_1, 32 bits wide
  assign and_1_out = reg1 & reg2;  // AND_Gate and_1, 32 bits wide
  assign or_1_out = reg1 | reg2;  // OR_Gate or_1, 32 bits wide
  assign nor_1_out = ~(reg1 | reg2);  // NOR_Gate nor_1, 32 bits wide
  Multiplier #(.width(32)) multiplier_1 (.a(reg1), .b(reg2), .out(multiplier_1_out));  // open: cin, cout
  Divider #(.width(32)) divider_1 (.a(reg1), .b(reg2), .out(divider_1_out));  // open: upper, rem
  Shifter #(.width(32)) shifter_1 (.in(reg2), .\dist (multiplexer_1_out), .out(shifter_1_out));
  Shifter #(.shift("lr"), .width(32)) shifter_2 (.in(reg2), .\dist (multiplexer_2_out), .out(shifter_2_out));
  Shifter #(.shift("ar"), .width(32)) shifter_3 (.in(reg2), .\dist (shiftAmount), .out(shifter_3_out));
  Comparator #(.width(32)) comparator_1 (.a(reg1), .b(reg2), .lt(comparator_1_lt[0]));  // open: gt, eq
  Multiplexer #(.select(4), .width(32)) multiplexer_3 (
    .in0(adder_1_out), .in1(undriven_3), .in2(subtractor_1_out), .in3(undriven_4), .in4(xor_1_out),
    .in5(and_1_out), .in6(or_1_out), .in7(nor_1_out), .in8(multiplier_1_out), .in9(divider_1_out),
    .in10(shifter_1_out), .in11(shifter_2_out), .in12(shifter_3_out), .in13(comparator_1_lt), .out(result),
    .sel(undriven_5));  // open: in14, in15

  // Notes on the sheet:
  //   inputs
  //   Adder
  //   Unsigned Adder
  //   Subtractor
  //   Unsigned Subtractor
  //   XOR
  //   AND
  //   OR
  //   NOR
  //   Multiplier
  //   Divider
  //   Logical Left
  //   Logical Right
  //   Arithmatic Right
  //   Comprator
  //   000000 for shiftAmount
  //   000100 for variable
  //   100000
  //   100000
  //   100010
  //   100010
  //   100110
  //   100100
  //   100101
  //   100111
  //   011000
  //   011010
  //   000010 for shiftAmount unsigned
  //   000110 for variable
  //   000011
  //   101010
  //   from control
endmodule
