// Logisim project cpu.circ as structural Verilog: 1 circuit, main circuit cpu
module cpu (
);

  wire isJAL, isRes, isWriteRD, not_1_out, syscall, WriteReg, zero;
  wire [1:0] PCcontrol;
  wire [3:0] Byte;
  wire [4:0] multiplexer_2_out, multiplexer_3_out;
  wire [25:0] ADD;
  wire [31:0] adder_1_out, DataMem_p4, imm32, multiplexer_4_out, nPC, PC, PC4, res, rsdata, rtdata,
       shifter_1_out, writedata;
  wire [31:26] INS;

  not not_1 (not_1_out, syscall);
  Shifter #(.width(32)) shifter_1 (.in(imm32), .\dist (5'b00010), .out(shifter_1_out));
  Register #(.width(32)) u_PC (.D(nPC), .en(not_1_out), .Q(PC));  // open: clk, clr
  Adder #(.width(32)) adder_1 (.a(PC4), .b(shifter_1_out), .out(adder_1_out));  // open: cin, cout
  Adder #(.width(32)) adder_2 (.a(PC), .b(32'h4), .out(PC4));  // open: cin, cout
  assign imm32 = {{16{ADD[15]}}, ADD[15:0]};  // Bit_Extender bit_extender_1
  Multiplexer #(.select(2), .width(32)) multiplexer_1 (
    .in0(PC4), .in1(adder_1_out), .in2(res), .in3({PC[31:28], ADD, 2'b00}), .out(nPC), .sel(PCcontrol));
  // mem InstMem: pin names not known; wires that end beside it: PC, 4'b0000, {32{1'b0}}, {INS, ADD}
  Multiplexer #(.width(5)) multiplexer_2 (.in0(ADD[20:16]), .in1(ADD[15:11]), .out(multiplexer_2_out), .sel(isWriteRD));
  Multiplexer #(.width(5)) multiplexer_3 (
    .in0(multiplexer_2_out), .in1({5{1'b1}}), .out(multiplexer_3_out), .sel(isJAL));
  Multiplexer #(.width(32)) multiplexer_4 (.in0(writedata), .in1(PC4), .out(multiplexer_4_out), .sel(isJAL));
  ALU_Control alu_control_1 (
    .reg1(rsdata), .reg2(rtdata), .shiftAmount(ADD[10:6]), .opcode(INS), .func(ADD[5:0]), .isRes(isRes),
    .isJAL(isJAL), .isWriteRD(isWriteRD), .syscall(syscall), .Byte(Byte), .WriteReg(WriteReg));
  // regfile RegisterFile: pin names not known; wires that end beside it: ADD[25:21], ADD[20:16], multiplexer_3_out, multiplexer_4_out, WriteReg, rsdata, rtdata
  ALU alu_1 (
    .rs(rsdata), .rt(rtdata), .imm(imm32), .shiftAmount(ADD[10:6]), .opcode(INS), .func(ADD[5:0]),
    .result(res), .zero(zero), .PCcontrol(PCcontrol));  // open: SatuControll
  // mem DataMem: pin names not known; wires that end beside it: res, Byte, rtdata, DataMem_p4
  Multiplexer #(.width(32)) multiplexer_5 (.in0(DataMem_p4), .in1(res), .out(writedata), .sel(isRes));

  // Other names for the same wires on the sheet: func[5:0] = ADD[5:0]; imm[15:0] = ADD[15:0]; INS[25:0] = ADD;
  //   sa[4:0] = ADD[10:6]; rd[4:0] = ADD[15:11]; rt[4:0] = ADD[20:16]; rs[4:0] = ADD[25:21]; OP[5:0] = INS

  // Notes on the sheet:
  //   PC Control
endmodule
